# Fritzing sketch nurseryman_wiring (saved by Fritzing 0.9.3b)
breadboards: 1

parts:
  micro-sd-kartenleser = MicroSD Card Module
  Bauteil2 = Arduino Uno (Rev3)
  BMP180 = Barometric Pressure Sensor - BMP180 Breakout (GY-68)
  DHT22 = Humidity and Temperature Sensor RHT03
  StepDown_Konverter = RioRand LM2596
  17HD4005 = Stepper Motor - Bipolar
  YL-69 = Soil Moisture Sensor
  Endschallter_rechts = Momentary Switch [package=tactile-pth]
  L298N = L298 [package=multiwatt15]
  Endschallter_links = Momentary Switch [package=tactile-pth]
  R1 = Resistor [tolerance=±5% resistance=100k package=THT]
  Tauchpumpe = DC Motor
  Schalltrelais = RELAY [package=relay-jzc]

nets:
  GND: micro-sd-kartenleser.GND, Bauteil2.GND, BMP180.GND, DHT22.GND_2, StepDown_Konverter.Pin_3, YL-69.GND, R1.Pin_1, Tauchpumpe.pin_1, Schalltrelais.MAIN
  VCC: micro-sd-kartenleser.VCC, DHT22.Vcc, StepDown_Konverter.Pin_2, YL-69.VCC, Endschallter_rechts.1, Endschallter_links.1, Schalltrelais.NO
  N1: micro-sd-kartenleser.MISO, Bauteil2.D6_PWM
  N2: micro-sd-kartenleser.MOSI, Bauteil2.D7
  N3: micro-sd-kartenleser.SCK, Bauteil2.D5_PWM
  N4: micro-sd-kartenleser.CS, Bauteil2.D13/SCK
  N5: Bauteil2.A4/SDA, BMP180.SDA
  N6: Bauteil2.A5/SCL, BMP180.SCL
  N7: Bauteil2.D8, L298N.IN1
  N8: Bauteil2.D9_PWM, L298N.IN2
  N9: Bauteil2.D10_PWM/SS, L298N.IN3
  N10: Bauteil2.D11_PWM/MOSI, L298N.IN4
  N11: Bauteil2.D12/MISO, Schalltrelais.COIL1
  N12: Bauteil2.D2, Endschallter_rechts.4, Endschallter_links.4, R1.Pin_0
  N13: Bauteil2.D3_PWM, YL-69.SIG
  N14: Bauteil2.D4, DHT22.Data-signal
  3V3: Bauteil2.3V3, BMP180.VCC
  N15: 17HD4005.A, L298N.OUT4
  N16: 17HD4005.C, L298N.OUT3
  N17: 17HD4005.B, L298N.OUT1
  N18: 17HD4005.D, L298N.OUT2
  N19: Tauchpumpe.pin_2, Schalltrelais.NC
